# Fritzing sketch controller_diag (saved by Fritzing 1.0.6)
breadboards: 1

parts:
  Part1 = Arduino Uno (Rev3) - ICSP
  RE1 = Rotary Encoder [package=THT]
  S1 = Pushbutton [package="[THT]"]
  S2 = Pushbutton [package="[THT]"]
  S3 = Pushbutton [package="[THT]"]
  S4 = Pushbutton [package="[THT]"]
  S5 = Pushbutton [package="[THT]"]
  M1 = OLED Mono 2.42 inch green
  Part2 = Bluetooth HC-05 Macho

nets:
  N1: Part1.D8, S5.Pin_3, S5.Pin_4
  N2: Part1.D9_PWM, M1.DC
  N3: Part1.D10_PWM/SS, M1.RES
  N4: Part1.D11_PWM/MOSI, M1.SDA
  N5: Part1.D12/MISO, M1.CS
  N6: Part1.D13/SCK, M1.SCL
  N7: Part1.D0/RX, Part2.TXD
  N8: Part1.D1/TX, Part2.RXD
  N9: Part1.D2, RE1.EncoderPinA
  N10: Part1.D3_PWM, RE1.EncoderPinB
  N11: Part1.D4, S1.Pin_3, S1.Pin_4
  N12: Part1.D5_PWM, S2.Pin_3, S2.Pin_4
  N13: Part1.D6_PWM, S3.Pin_3, S3.Pin_4
  N14: Part1.D7, S4.Pin_3, S4.Pin_4
  3V3: Part1.3V3, Part2.VCC
  5V: Part1.5V, M1.VCC
  GND: Part1.GND, RE1.EncoderPinC, S1.Pin_1, S1.Pin_2, S2.Pin_1, S2.Pin_2, S3.Pin_1, S3.Pin_2, S4.Pin_1, S4.Pin_2, S5.Pin_1, S5.Pin_2, M1.GND, Part2.GND

custom parts:
  OLED Mono 2.42 inch green: This is a 2.42 inch OLED display module of 128x64 resolution.
