# Fritzing sketch robot_diag (saved by Fritzing 1.0.6)

parts:
  Part1 = Arduino Mega ADK (Rev3)
  S1 = H-Bridge with L298N
  M1 = gear-motor
  M2 = gear-motor
  Module1 = Boladge HMC5883L Compass Module
  LED1 = smd LED [color="Red (633nm)" package="0805 [SMD]"]
  R1 = Resistor [tolerance=±5% resistance=220 package="2010 [SMD]"]
  Part2 = Bluetooth HC-05 Macho
  HC-SR04_Sensor_1 = HC-SR04 Ultrasonic Distance Sensor
  KY-1 = Keyes Relay [package=THT]
  USE_12V_LIPO = 4 x AAA Battery Mount [internal_resistance=0.1Ω]

nets:
  GND: Part1.GND, Module1.GND, LED1.anode, Part2.GND, HC-SR04_Sensor_1.GND
  N1: Part1.D13_PWM, KY-1.C
  N2: Part1.D12_PWM, S1.ENB
  N3: Part1.D11_PWM, S1.ENA
  N4: Part1.D10_PWM, Module1.DRDY
  N5: Part1.D9_PWM, HC-SR04_Sensor_1.TRIG
  N6: Part1.D8_PWM, HC-SR04_Sensor_1.ECHO
  VCC: Part1.3V3, Module1.VCC, Part2.VCC
  5V: Part1.5V, HC-SR04_Sensor_1.VCC
  N7: Part1.D0/RX0, Part2.TXD
  N8: Part1.D1/TX0, Part2.RXD
  N9: Part1.D2_PWM, S1.IN1
  N10: Part1.D3_PWM, S1.IN2
  N11: Part1.D4_PWM, S1.IN3
  N12: Part1.D5_PWM, S1.IN4
  N13: Part1.D6_PWM, R1.Pin_0
  N14: Part1.D7_PWM, Part2.State
  N15: S1.12V, KY-1.signal
  N16: S1.GND, KY-1.ground
  N17: S1.M1-01, M2.pin_1
  N18: S1.M1-02, M2.pin_2
  N19: S1.M2-01, M1.pin_2
  N20: S1.M2-02, M1.pin_1
  N21: KY-1.NC, USE_12V_LIPO.-
  N22: KY-1.NO, USE_12V_LIPO.+

custom parts:
  H-Bridge with L298N: h-bridge
  Boladge HMC5883L Compass Module: Cheap digital compass module
  Keyes Relay: The Keyes 5V relay module is suitable for SCM development, home appliance control. It uses a 5V~12V TIL control signal which can control DC / AC signal.
